# Fritzing sketch ARDUINO MEGA-UNO & ESP32 (I2C) (saved by Fritzing 0.9.10b)
breadboards: 1

parts:
  U1 = ESP32-38PinWide [part_number=ESP32-38PinWide]
  Componente1 = Arduino Uno (Rev3) - ICSP
  Componente2 = Arduino Mega ADK (Rev3)

nets:
  N1: U1.GPIO21, Componente1.A4/SDA, Componente2.D20/SDA
  N2: U1.GPIO22, Componente1.A5/SCL, Componente2.D21/SCL

custom parts:
  ESP32-38PinWide: Generic 38-Pin ESP32 with wide format (only access to one side of pins on a breadboard) based on Stephen Lilley's HiLetgo ESP-WROOM-32 ESP32 ESP-32S Development Board.
