# Fritzing sketch ARDUINO UNO ESCLAVO CON LCD (saved by Fritzing 0.9.10b)

parts:
  Componente1 = Arduino Uno (Rev3) - ICSP
  J1 = Basic Servo

nets:
  GND: Componente1.GND, J1.gnd
  N1: Componente1.D3_PWM, J1.pulse
