# Fritzing sketch sistema completo (saved by Fritzing 0.9.10b)
breadboards: 5

parts:
  Componente2 = Arduino Mega ADK (Rev3)
  HC-SR04_Sensor_2 = HC-SR04 Ultrasonic Distance Sensor
  HC-SR04_Sensor_3 = HC-SR04 Ultrasonic Distance Sensor
  HC-SR04_Sensor_4 = HC-SR04 Ultrasonic Distance Sensor
  R1 = Resistor [tolerance=±5% power=0.25 resistance=220 package=THT]
  R2 = Resistor [tolerance=±5% power=0.25 resistance=220 package=THT]
  R4 = Resistor [tolerance=±5% power=0.25 resistance=220 package=THT]
  LED1 = LED - 5mm [color="Red (633nm)" current=0.030 package="5 mm [THT]"]
  LED2 = LED - 5mm [color="Red (633nm)" current=0.030 package="5 mm [THT]"]
  LED4 = LED - 5mm [color="Red (633nm)" current=0.030 package="5 mm [THT]"]
  HC-SR04_Sensor_9 = HC-SR04 Ultrasonic Distance Sensor
  HC-SR04_Sensor_10 = HC-SR04 Ultrasonic Distance Sensor
  HC-SR04_Sensor_11 = HC-SR04 Ultrasonic Distance Sensor
  R9 = Resistor [tolerance=±5% power=0.25 resistance=220 package=THT]
  R10 = Resistor [tolerance=±5% power=0.25 resistance=220 package=THT]
  LED9 = LED - 5mm [color="Red (633nm)" current=0.030 package="5 mm [THT]"]
  LED10 = LED - 5mm [color="Red (633nm)" current=0.030 package="5 mm [THT]"]
  LED11 = LED - 5mm [color="Red (633nm)" current=0.030 package="5 mm [THT]"]
  R11 = Resistor [tolerance=±5% power=0.25 resistance=220 package=THT]
  HC-SR04_Sensor_12 = HC-SR04 Ultrasonic Distance Sensor
  HC-SR04_Sensor_13 = HC-SR04 Ultrasonic Distance Sensor
  HC-SR04_Sensor_14 = HC-SR04 Ultrasonic Distance Sensor
  R12 = Resistor [tolerance=±5% power=0.25 resistance=220 package=THT]
  R13 = Resistor [tolerance=±5% power=0.25 resistance=220 package=THT]
  LED12 = LED - 5mm [color="Red (633nm)" current=0.030 package="5 mm [THT]"]
  LED13 = LED - 5mm [color="Red (633nm)" current=0.030 package="5 mm [THT]"]
  LED14 = LED - 5mm [color="Red (633nm)" current=0.030 package="5 mm [THT]"]
  R14 = Resistor [tolerance=±5% power=0.25 resistance=220 package=THT]
  HC-SR04_Sensor_15 = HC-SR04 Ultrasonic Distance Sensor
  R15 = Resistor [tolerance=±5% power=0.25 resistance=220 package=THT]
  LED15 = LED - 5mm [color="Red (633nm)" current=0.030 package="5 mm [THT]"]
  HC-SR04_Sensor_16 = HC-SR04 Ultrasonic Distance Sensor
  R16 = Resistor [tolerance=±5% power=0.25 resistance=220 package=THT]
  LED16 = LED - 5mm [color="Red (633nm)" current=0.030 package="5 mm [THT]"]

nets:
  GND: Componente2.GND, HC-SR04_Sensor_2.GND, HC-SR04_Sensor_3.GND, HC-SR04_Sensor_4.GND, R1.Pin_0, R2.Pin_0, R4.Pin_1, HC-SR04_Sensor_9.GND, HC-SR04_Sensor_10.GND, HC-SR04_Sensor_11.GND, R9.Pin_0, R10.Pin_1, R11.Pin_0
  N1: Componente2.D2_PWM, HC-SR04_Sensor_3.TRIG
  N2: Componente2.D3_PWM, HC-SR04_Sensor_3.ECHO
  N3: Componente2.D4_PWM, LED1.anode
  N4: Componente2.D5_PWM, HC-SR04_Sensor_4.TRIG
  N5: Componente2.D6_PWM, HC-SR04_Sensor_4.ECHO
  N6: Componente2.D7_PWM, LED4.anode
  VCC: Componente2.5V, HC-SR04_Sensor_2.VCC, HC-SR04_Sensor_3.VCC, HC-SR04_Sensor_9.VCC, HC-SR04_Sensor_10.VCC, HC-SR04_Sensor_11.VCC
  N7: Componente2.D22, HC-SR04_Sensor_2.TRIG
  N8: Componente2.D23, HC-SR04_Sensor_9.TRIG
  N9: Componente2.D24, HC-SR04_Sensor_2.ECHO
  N10: Componente2.D25, HC-SR04_Sensor_9.ECHO
  N11: Componente2.D26, LED2.anode
  N12: Componente2.D27, LED9.anode
  N13: Componente2.D28, HC-SR04_Sensor_10.TRIG
  N14: Componente2.D29, HC-SR04_Sensor_11.TRIG
  N15: Componente2.D30, HC-SR04_Sensor_10.ECHO
  N16: Componente2.D31, HC-SR04_Sensor_11.ECHO
  N17: Componente2.D32, LED11.anode
  N18: Componente2.D33, LED10.anode
  N19: Componente2.D34, HC-SR04_Sensor_13.ECHO
  N20: Componente2.D35, HC-SR04_Sensor_14.ECHO
  N21: Componente2.D36, HC-SR04_Sensor_13.TRIG
  N22: Componente2.D37, HC-SR04_Sensor_14.TRIG
  N23: Componente2.D38, LED14.anode
  N24: Componente2.D39, LED13.anode
  N25: Componente2.D40, HC-SR04_Sensor_15.ECHO
  N26: Componente2.D41, HC-SR04_Sensor_12.ECHO
  N27: Componente2.D42, HC-SR04_Sensor_15.TRIG
  N28: Componente2.D43, HC-SR04_Sensor_12.TRIG
  N29: Componente2.D44, LED15.anode
  N30: Componente2.D45, LED12.anode
  N31: Componente2.D46, HC-SR04_Sensor_16.ECHO
  N32: Componente2.D48, HC-SR04_Sensor_16.TRIG
  N33: Componente2.D50/MISO, LED16.anode
  N34: R1.Pin_1, LED1.cathode
  N35: R2.Pin_1, LED2.cathode
  N36: R4.Pin_0, LED4.cathode
  N37: R9.Pin_1, LED11.cathode
  N38: R10.Pin_0, LED9.cathode
  N39: LED10.cathode, R11.Pin_1
  VCC_2: HC-SR04_Sensor_12.VCC, HC-SR04_Sensor_13.VCC, HC-SR04_Sensor_14.VCC, HC-SR04_Sensor_15.VCC, HC-SR04_Sensor_16.VCC
  GND_2: HC-SR04_Sensor_12.GND, HC-SR04_Sensor_13.GND, HC-SR04_Sensor_14.GND, R12.Pin_0, R13.Pin_1, R14.Pin_0, HC-SR04_Sensor_15.GND, R15.Pin_1, HC-SR04_Sensor_16.GND, R16.Pin_1
  N40: R12.Pin_1, LED14.cathode
  N41: R13.Pin_0, LED12.cathode
  N42: LED13.cathode, R14.Pin_1
  N43: R15.Pin_0, LED15.cathode
  N44: R16.Pin_0, LED16.cathode
